# Fritzing sketch Mudskip (saved by Fritzing 0.8.7b)
breadboards: 1

parts:
  SERVO1 = Tower Pro SG90 servo [part_number=101246]
  SERVO2 = Tower Pro SG90 servo [part_number=101246]
  SERVO3 = Tower Pro SG90 servo [part_number=101246]
  SERVO4 = Tower Pro SG90 servo [part_number=101246]
  Mod1 = Lipo Battery Pack
  U1 = ESP32S-HiLetgo [part_number=ESP32S-HiLetgo]
  Part1 = US-100 Ultrasonic Rangefinder

nets:
  N1: SERVO1.Signal, U1.GPIO25
  +5V: SERVO1.+5V, SERVO2.+5V, Mod1.+5V#2
  GND: SERVO1.GND, SERVO2.GND, SERVO3.GND, SERVO4.GND, Mod1.GND, U1.GND, Part1.GND, Part1.GND*
  N2: SERVO2.Signal, U1.GPIO26
  N3: SERVO3.Signal, U1.GPIO32
  +5V_2: SERVO3.+5V, SERVO4.+5V, Mod1.+5V#0, U1.VIN
  N4: SERVO4.Signal, U1.GPIO33
  N5: U1.3.3, Part1.VCC
  N6: U1.GPIO16, Part1.Echo/Rx
  N7: U1.GPIO17, Part1.Trig/Tx

notes:
  Left Horizontal Servo
  Left Vertical Servo
  Right Vertical Servo
  Right Horizontal Servo
  18650 Battery Shield
  US100 Ultrasonic Sensor
  ESP32 Devkit V1

custom parts:
  Tower Pro SG90 servo: Original file by John De Cristofaro http://www.adafruit.com/products/1449 Adafruit Feedback Servo (Small) Edited by: e-radionica.com 28/9/2015
  Lipo Battery Pack: Micro USB 5V 16340 18650 lithium Battery Shield V3 Wemos ESP32 ESP8266 Module
  ESP32S-HiLetgo: HiLetgo ESP-WROOM-32 ESP32 ESP-32S Development Board 2.4GHz Dual-Mode WiFi + Bluetooth Dual Cores Microcontroller The ESP32 integrated with Antenna switches, RF Balun, power amplifiers, low-noise amplifiers, filters, and management modules, and the entire solution occupies the least area of PCB. 2.4 GHz Wi-Fi plus Bluetooth dual-mode chip, with TSMC Ultra-low power consumption 40nm technology,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
